// Logisim project 1.circ as structural Verilog: 1 circuit, main circuit main
module main (
  input  X,
  input  Y,
  input  Z,
  output F
);

  wire AND1_out, AND2_out, AND3_out;

  and AND1 (AND1_out, X, Z);
  and AND2 (AND2_out, Y, X);
  and AND3 (AND3_out, Z, Y);
  or OR1 (F, AND1_out, AND2_out, AND3_out);
endmodule
